// Logisim project Pipelined Processor Design.circ as structural Verilog
module RegisterFile (
  input  [15:0] BusW,
  input  [2:0] RB,
  input  [2:0] RA,
  input  Clock,
  input  RegWrite,
  input  [2:0] RW,
  output [15:0] BusB,
  output [15:0] BusA
);

  wire _1_out, _2_out, _3_out, _4_out, _5_out, _6_out, _7_out, decoder_1_out1, decoder_1_out2,
       decoder_1_out3, decoder_1_out4, decoder_1_out5, decoder_1_out6, decoder_1_out7, decoder_2_out0,
       decoder_2_out1, decoder_2_out2, decoder_2_out3, decoder_2_out4, decoder_2_out5, decoder_2_out6,
       decoder_2_out7, decoder_3_out0, decoder_3_out1, decoder_3_out2, decoder_3_out3, decoder_3_out4,
       decoder_3_out5, decoder_3_out6, decoder_3_out7;
  wire [15:0] R1_q, R2_q, R3_q, R4_q, R5_q, R6_q, R7_q;

  Decoder #(.select(3)) decoder_1 (
    .out1(decoder_1_out1), .out2(decoder_1_out2), .out3(decoder_1_out3), .out4(decoder_1_out4),
    .out5(decoder_1_out5), .out6(decoder_1_out6), .out7(decoder_1_out7), .sel(RW), .en(1'b1));  // open: out0
  and _1 (_1_out, decoder_1_out1, RegWrite);
  and _2 (_2_out, decoder_1_out2, RegWrite);
  and _3 (_3_out, decoder_1_out3, RegWrite);
  and _4 (_4_out, decoder_1_out4, RegWrite);
  and _5 (_5_out, decoder_1_out5, RegWrite);
  and _6 (_6_out, decoder_1_out6, RegWrite);
  and _7 (_7_out, decoder_1_out7, RegWrite);
  Register #(.width(16)) R1 (.D(BusW), .en(_1_out), .Q(R1_q), .clk(Clock));  // open: clr
  Register #(.width(16)) R2 (.D(BusW), .en(_2_out), .Q(R2_q), .clk(Clock));  // open: clr
  Register #(.width(16)) R3 (.D(BusW), .en(_3_out), .Q(R3_q), .clk(Clock));  // open: clr
  Register #(.width(16)) R4 (.D(BusW), .en(_4_out), .Q(R4_q), .clk(Clock));  // open: clr
  Register #(.width(16)) R5 (.D(BusW), .en(_5_out), .Q(R5_q), .clk(Clock));  // open: clr
  Register #(.width(16)) R6 (.D(BusW), .en(_6_out), .Q(R6_q), .clk(Clock));  // open: clr
  Register #(.width(16)) R7 (.D(BusW), .en(_7_out), .Q(R7_q), .clk(Clock));  // open: clr
  assign BusA = decoder_2_out0 ? {16{1'b0}} : 16'bz;  // Controlled_Buffer controlled_buffer_1
  assign BusA = decoder_2_out2 ? R2_q : 16'bz;  // Controlled_Buffer controlled_buffer_2
  assign BusA = decoder_2_out1 ? R1_q : 16'bz;  // Controlled_Buffer controlled_buffer_3
  Decoder #(.select(3)) decoder_2 (
    .out0(decoder_2_out0), .out1(decoder_2_out1), .out2(decoder_2_out2), .out3(decoder_2_out3),
    .out4(decoder_2_out4), .out5(decoder_2_out5), .out6(decoder_2_out6), .out7(decoder_2_out7), .sel(RA),
    .en(1'b1));
  assign BusA = decoder_2_out6 ? R6_q : 16'bz;  // Controlled_Buffer controlled_buffer_4
  assign BusA = decoder_2_out5 ? R5_q : 16'bz;  // Controlled_Buffer controlled_buffer_5
  assign BusA = decoder_2_out4 ? R4_q : 16'bz;  // Controlled_Buffer controlled_buffer_6
  assign BusA = decoder_2_out3 ? R3_q : 16'bz;  // Controlled_Buffer controlled_buffer_7
  assign BusA = decoder_2_out7 ? R7_q : 16'bz;  // Controlled_Buffer controlled_buffer_8
  assign BusB = decoder_3_out0 ? {16{1'b0}} : 16'bz;  // Controlled_Buffer controlled_buffer_9
  assign BusB = decoder_3_out3 ? R3_q : 16'bz;  // Controlled_Buffer controlled_buffer_10
  assign BusB = decoder_3_out2 ? R2_q : 16'bz;  // Controlled_Buffer controlled_buffer_11
  assign BusB = decoder_3_out1 ? R1_q : 16'bz;  // Controlled_Buffer controlled_buffer_12
  Decoder #(.select(3)) decoder_3 (
    .out0(decoder_3_out0), .out1(decoder_3_out1), .out2(decoder_3_out2), .out3(decoder_3_out3),
    .out4(decoder_3_out4), .out5(decoder_3_out5), .out6(decoder_3_out6), .out7(decoder_3_out7), .sel(RB),
    .en(1'b1));
  assign BusB = decoder_3_out7 ? R7_q : 16'bz;  // Controlled_Buffer controlled_buffer_13
  assign BusB = decoder_3_out6 ? R6_q : 16'bz;  // Controlled_Buffer controlled_buffer_14
  assign BusB = decoder_3_out5 ? R5_q : 16'bz;  // Controlled_Buffer controlled_buffer_15
  assign BusB = decoder_3_out4 ? R4_q : 16'bz;  // Controlled_Buffer controlled_buffer_16

  // Notes on the sheet:
  //   STAGE 1
  //   STAGE 2
endmodule
